// Digital circuit 9NOR-OR.dig as structural Verilog
module _9NOR_OR (
  input  A,
  input  B,
  input  C,
  input  D,
  input  G,
  input  H,
  input  I,
  input  E,
  input  F,
  output OUT
);

  wire nor_1_out, nor_2_out, nor_3_out;

  nor nor_1 (nor_1_out, A, B, C);
  nor nor_2 (nor_2_out, D, E, F);
  nor nor_3 (nor_3_out, G, H, I);
  or or_1 (OUT, nor_1_out, nor_2_out, nor_3_out);
endmodule
