// Digital circuit AOI21.dig as structural Verilog
module AOI21 (
  input  A,
  input  B,
  input  C,
  output OUT
);

  wire and_1_out, or_1_out;

  and and_1 (and_1_out, A, B);
  or or_1 (or_1_out, and_1_out, C);
  not not_1 (OUT, or_1_out);
endmodule
