// Digital circuit DFF_ALR_CLK.dig as structural Verilog
module DFF_ALR_CLK (
  input  ALR,
  input  IN,
  input  CLK,
  output OUT
);

  wire multiplexer_1_out, multiplexer_2_out, nand_1_out, nand_2_out, not_1_out, not_3_out;

  nand nand_1 (nand_1_out, multiplexer_2_out, ALR);
  not not_1 (not_1_out, nand_1_out);
  Multiplexer multiplexer_1 (.sel(not_3_out), .in_0(nand_1_out), .in_1(nand_2_out), .out(multiplexer_1_out));
  nand nand_2 (nand_2_out, ALR, OUT);
  Multiplexer multiplexer_2 (.sel(not_3_out), .in_0(not_1_out), .in_1(IN), .out(multiplexer_2_out));
  not not_2 (OUT, multiplexer_1_out);
  not not_3 (not_3_out, CLK);
endmodule
