// Digital circuit dflipflip_active_low_reset.dig as structural Verilog
module dflipflip_active_low_reset (
  input  ALR,
  input  D,
  input  CLK,
  output OUT,
  output OUT_INV
);

  wire multiplexer_1_out, multiplexer_2_out, nand_2_out, not_1_out;

  Multiplexer multiplexer_1 (.sel(CLK), .in_0(D), .in_1(not_1_out), .out(multiplexer_1_out));
  nand nand_1 (OUT_INV, OUT, ALR);
  nand nand_2 (nand_2_out, ALR, multiplexer_1_out);
  not not_1 (not_1_out, nand_2_out);
  not not_2 (OUT, multiplexer_2_out);
  Multiplexer multiplexer_2 (.sel(CLK), .in_0(OUT_INV), .in_1(nand_2_out), .out(multiplexer_2_out));
endmodule
