// Digital circuit DFF_E.dig as structural Verilog
module DFF_E (
  input  CLK,
  input  DATA,
  output OUT
);

  wire multiplexer_1_out, multiplexer_2_out, not_1_out, not_2_out, not_3_out, not_5_out;

  not not_1 (not_1_out, multiplexer_2_out);
  not not_2 (not_2_out, not_1_out);
  Multiplexer multiplexer_1 (.sel(not_5_out), .in_0(not_1_out), .in_1(not_3_out), .out(multiplexer_1_out));
  not not_3 (not_3_out, OUT);
  not not_4 (OUT, multiplexer_1_out);
  Multiplexer multiplexer_2 (.sel(not_5_out), .in_0(not_2_out), .in_1(DATA), .out(multiplexer_2_out));
  not not_5 (not_5_out, CLK);

  // Notes on the sheet:
  //   (input bottom)
  //   (Input top)
endmodule
