// Digital circuit LATCH.dig as structural Verilog
module LATCH (
  input  IN,
  input  CLK,
  output out_3
);

  wire not_1_out, not_2_out;

  not not_1 (not_1_out, not_2_out);
  Multiplexer multiplexer_1 (.sel(CLK), .in_0(not_1_out), .in_1(IN), .out(out_3));
  not not_2 (not_2_out, out_3);
endmodule
