// Digital circuit OAI21.dig as structural Verilog
module OAI21 (
  input  A,
  input  B,
  input  C,
  output OUT
);

  wire and_1_out, or_1_out;

  or or_1 (or_1_out, A, B);
  and and_1 (and_1_out, or_1_out, C);
  not not_1 (OUT, and_1_out);
endmodule
